# Fritzing sketch 2022-12-06-test (saved by Fritzing 0.9.4)
breadboards: 1

parts:
  Composant1 = Arduino Uno (Rev3)
  C1 = Electrolytic Capacitor [capacitance=1000μF package="1010 [SMD, electrolytic]"]  # not connected
  Adafruit-12-neo = 12 NeoPixel Ring [part_number=1643]
  Adafruit-16-neo = 16 NeoPixel Ring [part_number=1463]
  R1 = Resistor [tolerance=±5% resistance=330 package="2512 [SMD]"]
  VCC1 = Battery
  Adafruit-8-neo-jewel = NeoPixel Jewel [part_number=2226]
  Composant2 = Adafruit Circuit Playground Express [part_number="Adafruit #3333"]  # not connected
  Touchwheel1 = Touchwheel  # not connected

nets:
  N1: Composant1.D6_PWM, R1.Pin_0
  GND: Composant1.GND, Adafruit-12-neo.GND, Adafruit-16-neo.GND, VCC1.-, Adafruit-8-neo-jewel.GND
  N2: Adafruit-12-neo.IN, Adafruit-16-neo.OUT
  N3: Adafruit-12-neo.OUT, Adafruit-8-neo-jewel.IN
  N4: Adafruit-16-neo.IN, R1.Pin_1
  N5: Adafruit-16-neo.VDD, VCC1.+

notes:
  Before connecting NeoPixels to any large power source (DC “wall wart” or even a large battery), add a capacitor (500–1000 µF at 6.3V or higher) across the + and – terminals as shown above. The capacitor buffers sudden changes in the current drawn by the strip.
  for wearable projects — a 3.7 Volt lithium-polymer battery.
  If using a 3.3V microcontroller, it’s wise to use a logic level shifter
  Place a 300 to 500 Ohm resistor between the Arduino data output pin and the input to the first NeoPixel. The resistor should be at the end of the wire closest to the NeoPixel(s), not the microcontroller.
  Nothing’s needed at the “out” end of a strip…you can leave the data out “floating.

custom parts:
  12 NeoPixel Ring: 12 ultra bright smart LED NeoPixels are arranged in a circle with 1.5" (37mm) outer diameter. The rings are 'chainable' - connect the output pin of one to the input pin of another. Use only one microcontroller pin to control as many as you can chain together! Each LED is addressable as the driver chip is inside the LED. Each one has ~18mA constant current drive so the color will be very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
  16 NeoPixel Ring: 16 ultra bright smart LED NeoPixels are arranged in a circle with 1.75" (44.5mm) outer diameter. The rings are 'chainable' - connect the output pin of one to the input pin of another. Use only one microcontroller pin to control as many as you can chain together! Each LED is addressable as the driver chip is inside the LED. Each one has ~18mA constant current drive so the color will be very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
  NeoPixel Jewel: We fit seven of our tiny 5050 (5mm x 5mm) smart RGB LEDs onto a beautiful, round PCB with mounting holes and a chainable design to create what we think is our most elegant (and evening-wear appropriate) NeoPixel board yet. Use only one microcontroller pin to control as many as you can chain together! Each LED is addressable as the driver chip is inside the LED. Each one has ~18mA constant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
  Adafruit Circuit Playground Express: Circuit Playground Express is the next step towards a perfect introduction to electronics and programming. We've taken the original Circuit Playground Classic and made it even better! Not only did we pack even more sensors in, we also made it even easier to program. You can now start your journey with Microsoft MakeCode block-based or Javascript programming. Then, you can use the same board to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
