# Fritzing sketch wheelpad-led-2022-12-12 (saved by Fritzing 0.9.4)
breadboards: 1

parts:
  Touchwheel1 = Touchwheel
  Composant1 = Adafruit MPR121
  R1 = Resistor [tolerance=±5% resistance=220 package="2010 [SMD]"]
  R2 = Resistor [tolerance=±5% resistance=220 package="2010 [SMD]"]
  R3 = Resistor [tolerance=±5% resistance=220 package="2010 [SMD]"]
  LED1 = RGB LED (com. cathode, rgb) [package="5 mm [THT]"]
  Composant2 = Arduino Uno (Rev3)

nets:
  N1: Touchwheel1.11, Composant1.ELEC11
  N2: Touchwheel1.4, Composant1.ELEC4
  N3: Touchwheel1.1, Composant1.ELEC1
  N4: Touchwheel1.8, Composant1.ELEC8
  N5: Touchwheel1.2, Composant1.ELEC2
  N6: Touchwheel1.5, Composant1.ELEC5
  N7: Touchwheel1.0, Composant1.ELEC0
  N8: Touchwheel1.3, Composant1.ELEC3
  N9: Touchwheel1.7, Composant1.ELEC7
  N10: Touchwheel1.9, Composant1.ELEC9
  N11: Touchwheel1.10, Composant1.ELEC10
  N12: Touchwheel1.6, Composant1.ELEC6
  GND: Composant1.GND, LED1.common_cathode, Composant2.GND
  3.3V: Composant1.3.3V, Composant2.3V3
  N13: Composant1.SDA, Composant2.A4/SDA
  N14: Composant1.SCL, Composant2.A5/SCL
  N15: Composant1.IRQ, Composant2.D2
  N16: R1.Pin_0, Composant2.D10_PWM/SS
  N17: R1.Pin_1, LED1.green_anode
  N18: R2.Pin_0, Composant2.D11_PWM/MOSI
  N19: R2.Pin_1, LED1.blue_anode
  N20: R3.Pin_0, Composant2.D9_PWM
  N21: R3.Pin_1, LED1.red_anode

custom parts:
  Adafruit MPR121: Add lots of touch sensors to your next microcontroller project with this easy-to-use 12-channel capacitive touch sensor breakout board, starring the MPR121. This chip can handle up to 12 individual touch pads. The MPR121 has support for only I2C, which can be implemented with nearly any microcontroller. You can select one of 4 addresses with the ADDR pin, for a total of 48 capacitive touch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
