# Fritzing sketch schematics-2023-01-14 (saved by Fritzing 0.9.4)
breadboards: 1

parts:
  BRIGHTNESS_POT = Rotary Potentiometer (Small) [maximum_resistance=100kΩ package=THT]
  R6 = Resistor [tolerance=±5% resistance=220 package="2010 [SMD]"]
  R7 = Resistor [tolerance=±5% resistance=220 package="2010 [SMD]"]
  Circuit_Playground = Adafruit Circuit Playground Express [part_number="Adafruit #3333"]
  Capacitive_Touchwheel = Touchwheel
  RING0_32_LEDS = Neopixel Strip -- Black (30/m) [part_number=1376]
  C2 = Electrolytic Capacitor [capacitance=1mF voltage=16V package="0807 [SMD, electrolytic]"]
  MPR121 = MPR121 Breakout
  RING1_24_LEDS = Neopixel Strip -- Black (30/m) [part_number=1376]
  RING2_16_LEDS = Neopixel Strip -- Black (30/m) [part_number=1376]
  RING3_12_LEDS = Neopixel Strip -- Black (30/m) [part_number=1376]
  RING5_1_LED = Neopixel Strip -- Black (30/m) [part_number=1376]
  RING4_8_LEDS = Neopixel Strip -- Black (30/m) [part_number=1376]

nets:
  N1: BRIGHTNESS_POT.leg1, Circuit_Playground.VOUT, RING0_32_LEDS.+5V#3, C2.+, MPR121.3.3V
  N2: BRIGHTNESS_POT.wiper, Circuit_Playground.D10_A3
  GND: BRIGHTNESS_POT.leg2, Circuit_Playground.GND, RING0_32_LEDS.GND#1, C2.-, MPR121.GND
  N3: R6.Pin_0, R7.Pin_0
  N4: R6.Pin_1, Circuit_Playground.D9_A2
  N5: R7.Pin_1, RING0_32_LEDS.Din
  N6: Circuit_Playground.D6_A1, MPR121.~IRQ
  N7: Circuit_Playground.D3_A4_SCL, MPR121.SCL
  N8: Circuit_Playground.D2_A5_SDA, MPR121.SDA
  N9: Capacitive_Touchwheel.11, MPR121.ELE11
  N10: Capacitive_Touchwheel.4, MPR121.ELE4
  N11: Capacitive_Touchwheel.1, MPR121.ELE1
  N12: Capacitive_Touchwheel.8, MPR121.ELE8
  N13: Capacitive_Touchwheel.2, MPR121.ELE2
  N14: Capacitive_Touchwheel.5, MPR121.ELE5
  N15: Capacitive_Touchwheel.0, MPR121.ELE0
  N16: Capacitive_Touchwheel.3, MPR121.ELE3
  N17: Capacitive_Touchwheel.7, MPR121.ELE7
  N18: Capacitive_Touchwheel.9, MPR121.ELE9
  N19: Capacitive_Touchwheel.10, MPR121.ELE10
  N20: Capacitive_Touchwheel.6, MPR121.ELE6
  N21: RING0_32_LEDS.+5V#4, RING1_24_LEDS.+5V#3
  N22: RING0_32_LEDS.Dout, RING1_24_LEDS.Din
  N23: RING0_32_LEDS.GND#6, RING1_24_LEDS.GND#1
  N24: RING1_24_LEDS.+5V#4, RING2_16_LEDS.+5V#3
  N25: RING1_24_LEDS.Dout, RING2_16_LEDS.Din
  N26: RING1_24_LEDS.GND#6, RING2_16_LEDS.GND#1
  N27: RING2_16_LEDS.+5V#4, RING3_12_LEDS.+5V#3
  N28: RING2_16_LEDS.Dout, RING3_12_LEDS.Din
  N29: RING2_16_LEDS.GND#6, RING3_12_LEDS.GND#1
  N30: RING3_12_LEDS.+5V#4, RING4_8_LEDS.+5V#3
  N31: RING3_12_LEDS.Dout, RING4_8_LEDS.Din
  N32: RING3_12_LEDS.GND#6, RING4_8_LEDS.GND#1
  N33: RING5_1_LED.GND, RING4_8_LEDS.GND#6
  N34: RING5_1_LED.Din, RING4_8_LEDS.Dout
  N35: RING5_1_LED.+5V, RING4_8_LEDS.+5V#4

notes:
  Potentiometer for user to adjust brightness
  my real part doesnt exist
  it is normally:
  93 LEDs WS2812B RGB 6 Ring Lamp
  Operating Voltage: 5V
  Operating Current: ≤1A
  LED Type: WS2812B
  LED Quantity: 93
  Color: Full Color RGB
  Source: https://www.dfrobot.com/product-2091.html
  This is supposed to be a Proto Gizmo
  https://www.adafruit.com/product/4320

custom parts:
  Adafruit Circuit Playground Express: Circuit Playground Express is the next step towards a perfect introduction to electronics and programming. We've taken the original Circuit Playground Classic and made it even better! Not only did we pack even more sensors in, we also made it even easier to program. You can now start your journey with Microsoft MakeCode block-based or Javascript programming. Then, you can use the same board to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
  Neopixel Strip -- Black (30/m): These NeoPixel strips have 30 digitally-addressable pixel LEDs per meter and are very affordable and are only 12.5 mm wide, 10 mm if you remove the strip from the casing.
