# Fritzing sketch schematics-2023-01-05 (saved by Fritzing 0.9.4)
breadboards: 1

parts:
  Touchwheel1 = Touchwheel
  Composant1 = Adafruit MPR121
  R2 = Resistor [tolerance=±5% resistance=220 package="2010 [SMD]"]
  R3 = Resistor [tolerance=±5% resistance=220 package="2010 [SMD]"]
  Composant2 = Arduino Uno (Rev3)
  R4 = Rotary Potentiometer (Small) [maximum_resistance=100kΩ package=THT]
  C1 = Electrolytic Capacitor [capacitance=1mF voltage=16V package="0807 [SMD, electrolytic]"]
  Composant4 = 16 NeoPixel Ring [part_number=1463]
  Composant5 = 24 NeoPixel Ring [part_number=1586]
  Composant6 = 12 NeoPixel Ring [part_number=1643]
  Composant7 = NeoPixel Jewel [part_number=2226]

nets:
  N1: Touchwheel1.11, Composant1.ELEC11
  N2: Touchwheel1.4, Composant1.ELEC4
  N3: Touchwheel1.1, Composant1.ELEC1
  N4: Touchwheel1.8, Composant1.ELEC8
  N5: Touchwheel1.2, Composant1.ELEC2
  N6: Touchwheel1.5, Composant1.ELEC5
  N7: Touchwheel1.0, Composant1.ELEC0
  N8: Touchwheel1.3, Composant1.ELEC3
  N9: Touchwheel1.7, Composant1.ELEC7
  N10: Touchwheel1.9, Composant1.ELEC9
  N11: Touchwheel1.10, Composant1.ELEC10
  N12: Touchwheel1.6, Composant1.ELEC6
  GND: Composant1.GND, Composant2.GND, R4.leg2, C1.+, Composant4.GND, Composant5.GND, Composant6.GND, Composant7.GND
  VDD: Composant1.VIN, Composant2.5V, R4.leg1, C1.-, Composant4.VDD, Composant5.VDD, Composant6.VDD, Composant7.VDD
  N13: Composant1.SDA, Composant2.A4/SDA
  N14: Composant1.SCL, Composant2.A5/SCL
  N15: Composant1.IRQ, Composant2.D2
  N16: R2.Pin_0, R3.Pin_0
  N17: R2.Pin_1, Composant5.IN
  N18: R3.Pin_1, Composant2.D6_PWM
  N19: Composant2.A1, R4.wiper
  N20: Composant4.IN, Composant5.OUT
  N21: Composant4.OUT, Composant6.IN
  N22: Composant6.OUT, Composant7.IN

notes:
  Potentiometer for user to adjust brightness
  my real part doesnt exist
  it is normally:
  93 LEDs WS2812B RGB 6 Ring Lamp
  Operating Voltage: 5V
  Operating Current: ≤1A
  LED Type: WS2812B
  LED Quantity: 93
  Color: Full Color RGB
  Source: https://www.dfrobot.com/product-2091.html
  Capacitive Touch scrollwheel:
  If using circuit express, possibly i wont use this

custom parts:
  Adafruit MPR121: Add lots of touch sensors to your next microcontroller project with this easy-to-use 12-channel capacitive touch sensor breakout board, starring the MPR121. This chip can handle up to 12 individual touch pads. The MPR121 has support for only I2C, which can be implemented with nearly any microcontroller. You can select one of 4 addresses with the ADDR pin, for a total of 48 capacitive touch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
  16 NeoPixel Ring: 16 ultra bright smart LED NeoPixels are arranged in a circle with 1.75" (44.5mm) outer diameter. The rings are 'chainable' - connect the output pin of one to the input pin of another. Use only one microcontroller pin to control as many as you can chain together! Each LED is addressable as the driver chip is inside the LED. Each one has ~18mA constant current drive so the color will be very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
  24 NeoPixel Ring: 24 ultra bright smart LED NeoPixels are arranged in a circle with 2.6" (66mm) outer diameter. The rings are 'chainable' - connect the output pin of one to the input pin of another. Use only one microcontroller pin to control as many as you can chain together! Each LED is addressable as the driver chip is inside the LED. Each one has ~18mA constant current drive so the color will be very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
  12 NeoPixel Ring: 12 ultra bright smart LED NeoPixels are arranged in a circle with 1.5" (37mm) outer diameter. The rings are 'chainable' - connect the output pin of one to the input pin of another. Use only one microcontroller pin to control as many as you can chain together! Each LED is addressable as the driver chip is inside the LED. Each one has ~18mA constant current drive so the color will be very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
  NeoPixel Jewel: We fit seven of our tiny 5050 (5mm x 5mm) smart RGB LEDs onto a beautiful, round PCB with mounting holes and a chainable design to create what we think is our most elegant (and evening-wear appropriate) NeoPixel board yet. Use only one microcontroller pin to control as many as you can chain together! Each LED is addressable as the driver chip is inside the LED. Each one has ~18mA constant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
