# Fritzing sketch schematics-2023-01-06 (saved by Fritzing 0.9.4)
breadboards: 2

parts:
  Touchwheel1 = Touchwheel
  Composant1 = Adafruit MPR121
  R2 = Resistor [tolerance=±5% resistance=220 package="2010 [SMD]"]
  R3 = Resistor [tolerance=±5% resistance=220 package="2010 [SMD]"]
  Composant2 = Arduino Uno (Rev3)
  R4 = Rotary Potentiometer (Small) [maximum_resistance=100kΩ package=THT]
  C1 = Electrolytic Capacitor [capacitance=1mF voltage=16V package="0807 [SMD, electrolytic]"]
  Composant4 = 16 NeoPixel Ring [part_number=1463]
  Composant5 = 24 NeoPixel Ring [part_number=1586]
  Composant6 = 12 NeoPixel Ring [part_number=1643]
  Composant7 = NeoPixel Jewel [part_number=2226]
  Composant9 = 24 NeoPixel Ring [part_number=1586]
  Composant10 = 16 NeoPixel Ring [part_number=1463]
  Composant11 = 12 NeoPixel Ring [part_number=1643]
  R5 = Rotary Potentiometer (Small) [maximum_resistance=100kΩ package=THT]
  C2 = Electrolytic Capacitor [capacitance=1mF voltage=16V package="0807 [SMD, electrolytic]"]
  R6 = Resistor [tolerance=±5% resistance=220 package="2010 [SMD]"]
  R7 = Resistor [tolerance=±5% resistance=220 package="2010 [SMD]"]
  Composant13 = NeoPixel Jewel [part_number=2226]
  U1 = TOUCH [package=touch1]
  U2 = TOUCH [package=touch1]  # not connected
  U3 = TOUCH [package=touch1]
  U4 = TOUCH [package=touch1]
  U5 = TOUCH [package=touch1]
  U6 = TOUCH [package=touch1]
  Composant15 = Lithium Ion Polymer Battery 3.7v 350mAh [part_number=2750]  # not connected
  Composant19 = Lithium Ion Polymer Battery 3.7v 500mAh [part_number=1578]  # not connected
  Composant14 = Adafruit Circuit Playground Express [part_number="Adafruit #3333"]

nets:
  N1: Touchwheel1.11, Composant1.ELEC11
  N2: Touchwheel1.4, Composant1.ELEC4
  N3: Touchwheel1.1, Composant1.ELEC1
  N4: Touchwheel1.8, Composant1.ELEC8
  N5: Touchwheel1.2, Composant1.ELEC2
  N6: Touchwheel1.5, Composant1.ELEC5
  N7: Touchwheel1.0, Composant1.ELEC0
  N8: Touchwheel1.3, Composant1.ELEC3
  N9: Touchwheel1.7, Composant1.ELEC7
  N10: Touchwheel1.9, Composant1.ELEC9
  N11: Touchwheel1.10, Composant1.ELEC10
  N12: Touchwheel1.6, Composant1.ELEC6
  GND: Composant1.GND, Composant2.GND, R4.leg2, C1.+, Composant4.GND, Composant5.GND, Composant6.GND, Composant7.GND
  VDD: Composant1.VIN, Composant2.5V, R4.leg1, C1.-, Composant4.VDD, Composant5.VDD, Composant6.VDD, Composant7.VDD
  N13: Composant1.SDA, Composant2.A4/SDA
  N14: Composant1.SCL, Composant2.A5/SCL
  N15: Composant1.IRQ, Composant2.D2
  N16: R2.Pin_0, R3.Pin_0
  N17: R2.Pin_1, Composant5.IN
  N18: R3.Pin_1, Composant2.D6_PWM
  N19: Composant2.A1, R4.wiper
  N20: Composant4.IN, Composant5.OUT
  N21: Composant4.OUT, Composant6.IN
  N22: Composant6.OUT, Composant7.IN
  N23: Composant9.IN, R7.Pin_1
  N24: Composant9.OUT, Composant10.IN
  VDD_2: Composant9.VDD, Composant10.VDD, Composant11.VDD, R5.leg1, C2.-, Composant13.VDD, Composant14.VOUT
  GND_2: Composant9.GND, Composant10.GND, Composant11.GND, R5.leg2, C2.+, Composant13.GND, Composant14.GND
  N25: Composant10.OUT, Composant11.IN
  N26: Composant11.OUT, Composant13.IN
  N27: R5.wiper, Composant14.D9_A2
  N28: R6.Pin_0, R7.Pin_0
  N29: R6.Pin_1, Composant14.D6_A1
  N30: U1.T2, Composant14.D10_A3
  N31: U3.T2, U6.T1, Composant14.D0_A6_RX
  N32: U4.T2, Composant14.D1_A7_TX
  N33: U5.T2, Composant14.D3_A4_SCL
  N34: U6.T2, Composant14.D2_A5_SDA

notes:
  Potentiometer for user to adjust brightness
  my real part doesnt exist
  it is normally:
  93 LEDs WS2812B RGB 6 Ring Lamp
  Operating Voltage: 5V
  Operating Current: ≤1A
  LED Type: WS2812B
  LED Quantity: 93
  Color: Full Color RGB
  Source: https://www.dfrobot.com/product-2091.html
  Capacitive Touch scrollwheel:
  If using circuit express, possibly i wont use this
  Notes about Circuit Express pins:
  Vout - there is one Voltage Output pad. This is a special power pad, it will be connected to either the USB power or the battery input, whichever has the higher voltage. This output does not connect to the regulator so you can draw as much current as your USB port / Battery can provide. There is a resettable fuse on this pin, so you can draw about 500mA continuous, and 1 Amp peak before it will trip. If the fuse trips, just wait a minute and it will automatically reset
  If you want to connect servos, NeoPixels, DotStars or other high power electronics that are OK up to 5V, use the Vout pad.
  All of the GPIO pads are 3.3V output level, and should not be used with 5V inputs. In general, most 5V devices are OK with 3.3V output though.
  Each Pin!
  Let's start with A0 which is in the bottom right corner, and work our way counter-clockwise
  A0 (a.k.a D12) - This is a special pin that can do true analog output so it's great for playing audio clips. In can be digital I/O, or analog I/O, but if you do that it will interfere with the built-in speaker. This is the one pin that cannot be used for capacitive touch.
  A1 / D6 - This pin can be digital I/O, or analog Input. This pin has PWM output and can be capacitive touch sensor
  A2 / D9 - This pin can be digital I/O, or analog Input. This pin has PWM output and can be capacitive touch sensor
  A3 / D10 - This pin can be digital I/O, or analog Input. This pin has PWM output and can be capacitive touch sensor
  A4 / D3 - This pin can be digital I/O, or analog Input. This pin is also the I2C SCL pin, and can be capacitive touch sensor
  A5 / D2 - This pin can be digital I/O, or analog Input. This pin is also the I2C SDA pin, and can be capacitive touch sensor
  A6 / D0 - This pin can be digital I/O, or analog Input. This pin has PWM output, Serial Receive, and can be capacitive touch sensor
  A7 / D1 - This pin can be digital I/O, or analog Input. This pin has PWM output, Serial Transmit, and can be capacitive touch sensor
  D4 - Left Button A
  D5 - Right Button B
  D7 - Slide Switch
  D8 - Built-in 10 NeoPixels
  D13 - Red LED
  D27 - Accelerometer interrupt
  D25 - IR Transmitter
  D26 - IR Receiver
  A0 - Speaker analog output
  A8 - Light Sensor
  A9 - Temperature Sensor
  A10 - IR Proximity Sensor
  D28 - Internal I2C SDA (access with Wire1)
  D29 - Internal I2C SCL (access with Wire1)
  D30 (PIN_SPI_MISO) - SPI FLASH MISO
  D31 (PIN_SPI_SCK) - SPI FLASH SCK
  D32 (PIN_SPI_MOSI) - SPI FLASH MOSI
  D33 - SPI FLASH Chip Select

custom parts:
  Adafruit MPR121: Add lots of touch sensors to your next microcontroller project with this easy-to-use 12-channel capacitive touch sensor breakout board, starring the MPR121. This chip can handle up to 12 individual touch pads. The MPR121 has support for only I2C, which can be implemented with nearly any microcontroller. You can select one of 4 addresses with the ADDR pin, for a total of 48 capacitive touch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
  16 NeoPixel Ring: 16 ultra bright smart LED NeoPixels are arranged in a circle with 1.75" (44.5mm) outer diameter. The rings are 'chainable' - connect the output pin of one to the input pin of another. Use only one microcontroller pin to control as many as you can chain together! Each LED is addressable as the driver chip is inside the LED. Each one has ~18mA constant current drive so the color will be very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
  24 NeoPixel Ring: 24 ultra bright smart LED NeoPixels are arranged in a circle with 2.6" (66mm) outer diameter. The rings are 'chainable' - connect the output pin of one to the input pin of another. Use only one microcontroller pin to control as many as you can chain together! Each LED is addressable as the driver chip is inside the LED. Each one has ~18mA constant current drive so the color will be very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
  12 NeoPixel Ring: 12 ultra bright smart LED NeoPixels are arranged in a circle with 1.5" (37mm) outer diameter. The rings are 'chainable' - connect the output pin of one to the input pin of another. Use only one microcontroller pin to control as many as you can chain together! Each LED is addressable as the driver chip is inside the LED. Each one has ~18mA constant current drive so the color will be very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
  NeoPixel Jewel: We fit seven of our tiny 5050 (5mm x 5mm) smart RGB LEDs onto a beautiful, round PCB with mounting holes and a chainable design to create what we think is our most elegant (and evening-wear appropriate) NeoPixel board yet. Use only one microcontroller pin to control as many as you can chain together! Each LED is addressable as the driver chip is inside the LED. Each one has ~18mA constant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
  Lithium Ion Polymer Battery 3.7v 350mAh: Lithium ion polymer (also known as 'lipo' or 'lipoly') batteries are thin, light and powerful. The output ranges from 4.2V when completely charged to 3.7V. This battery has a capacity of 350mAh for a total of about 1.3 Wh. The batteries come pre-attached with a genuine 2-pin JST-PH connector as shown and include the necessary protection circuitry.
  Lithium Ion Polymer Battery 3.7v 500mAh: Lithium ion polymer (also known as 'lipo' or 'lipoly') batteries are thin, light and powerful. The output ranges from 4.2V when completely charged to 3.7V. This battery has a capacity of 500mAh for a total of about 1.9 Wh. The batteries come pre-attached with a genuine 2-pin JST-PH connector as shown and include the necessary protection circuitry.
  Adafruit Circuit Playground Express: Circuit Playground Express is the next step towards a perfect introduction to electronics and programming. We've taken the original Circuit Playground Classic and made it even better! Not only did we pack even more sensors in, we also made it even easier to program. You can now start your journey with Microsoft MakeCode block-based or Javascript programming. Then, you can use the same board to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
